// Logisim project offline-1_tmp1.circ as structural Verilog: 1 circuit, main circuit main
module main (
  input  S2,
  input  S1,
  input  S0,
  input  A3,
  input  A2,
  input  A1,
  input  A0,
  input  B3,
  input  B2,
  input  B1,
  input  B0,
  output F3,
  output F2,
  output F1,
  output F0,
  output C,
  output V,
  output Z,
  output S,
  output F3_2,
  output F2_2,
  output F1_2,
  output F0_2,
  output C_2,
  output V_2,
  output Z_2,
  output S_2
);

  wire n7400_1_p3, n7400_1_p4, n7400_1_p7, n7400_1_p12, n7400_1_p15, n7408_1_p3, n7408_1_p6, n7408_1_p11,
       n7408_1_p14, n7408_2_p3, n7408_2_p6, n7408_2_p9, n7408_2_p10, n7432_1_p3, n7432_1_p6, n7432_1_p11,
       n7432_1_p14, n7432_2_p3, n7432_2_p6, n7432_2_p11, n7486_1_p3, n7486_1_p6, n7486_1_p12, n7486_3_p6,
       n7486_3_p9, n74157_1_p4, n74157_1_p7, n74157_1_p13, n74157_1_p16, n74157_2_p3, n74157_2_p4,
       n74157_2_p6, n74157_2_p7, n74157_2_p12, n74157_2_p13, n74157_2_p15, n74157_2_p16;

  // _7408 7408_1: pin names not known; wires that end beside it: S1, B0, n7408_1_p3, S1, B1, n7408_1_p6, 1'b0, 1'b1, S1, B3, n7408_1_p11, S1, B2, n7408_1_p14
  // _7400 7400_1: pin names not known; wires that end beside it: B1, B0, n7400_1_p3, n7400_1_p4, B1, n7400_1_p3, n7400_1_p7, 1'b0, 1'b1, n7400_1_p3, B3, n7400_1_p12, n7400_1_p3, B2, n7400_1_p15
  // _7432 7432_1: pin names not known; wires that end beside it: n7408_1_p3, A0, n7432_1_p3, n7408_1_p6, A1, n7432_1_p6, 1'b0, 1'b1, n7408_1_p11, A3, n7432_1_p11, n7408_1_p14, A2, n7432_1_p14
  // _7486 7486_1: pin names not known; wires that end beside it: S0, S1, n7486_1_p3, S0, 1'b1, n7486_1_p6, 1'b0, 1'b1, S1, S2, n7400_1_p3, n7486_1_p12, 1'b1, Z
  // _74157 74157_1: pin names not known; wires that end beside it: S0, 1'b1, n7400_1_p4, n74157_1_p4, 1'b1, n7400_1_p7, n74157_1_p7, 1'b0, 1'b1, 1'b0, 1'b1, n7400_1_p12, n74157_1_p13, 1'b1, n7400_1_p15, n74157_1_p16
  // _7408 7408_2: pin names not known; wires that end beside it: S1, S2, n7408_2_p3, n7486_1_p6, S1, n7408_2_p6, 1'b0, 1'b1, n7408_2_p9, n7408_2_p10, C
  // _74157 74157_2: pin names not known; wires that end beside it: S0, n7432_1_p3, n74157_2_p3, n74157_2_p4, n7432_1_p6, n74157_2_p6, n74157_2_p7, 1'b0, 1'b1, 1'b0, n7432_1_p11, n74157_2_p12, n74157_2_p13, n7432_1_p14, n74157_2_p15, n74157_2_p16
  // _7486 7486_2: pin names not known; wires that end beside it: A0, n7408_2_p3, n74157_2_p3, A1, n7408_2_p3, n74157_2_p6, 1'b0, 1'b1, A3, n7408_2_p3, n74157_2_p12, A2, n7408_2_p3, n74157_2_p15
  // _7432 7432_2: pin names not known; wires that end beside it: n7486_1_p3, n7408_2_p3, n7432_2_p3, F3, F2, n7432_2_p6, 1'b0, 1'b1, n7432_2_p6, F1, n7432_2_p11, n7432_2_p11, F0, n7486_1_p12
  // adderseparate_main main_1: pin names not known; wires that end beside it: n74157_2_p13, F2, n74157_2_p16, n74157_1_p16, 1'b1, F1, n74157_1_p7, n74157_2_p7, n74157_1_p13, F3, n7408_2_p9, n7432_2_p3, 1'b0, n74157_1_p4, n74157_2_p4, F0
  // _7486 7486_3: pin names not known; wires that end beside it: n7408_2_p6, 1'b1, n7408_2_p10, n74157_2_p13, n74157_1_p13, n7486_3_p6, 1'b0, 1'b1, n7486_3_p9, n7408_2_p9, V, F3, n7486_3_p6, n7486_3_p9

  assign C_2 = C;
  assign F0_2 = F0;
  assign F1_2 = F1;
  assign F2_2 = F2;
  assign F3_2 = F3;
  assign S = F3;
  assign S_2 = F3;
  assign V_2 = V;
  assign Z_2 = Z;
endmodule
