// Logisim project offline-1.circ as structural Verilog: 1 circuit, main circuit main
module main (
  input  S2,
  input  S1,
  input  S0,
  input  A3,
  input  A2,
  input  A1,
  input  A0,
  input  B3,
  input  B2,
  input  B1,
  input  B0
);

  wire n7408_1_p3, n7408_1_p6, n7408_1_p10, n7408_1_p13, n7408_2_p3, n7432_1_p3, n7432_1_p6, n7432_1_p10,
       n7432_1_p13, n7432_2_p3, n7486_1_p3, n74157_1_p3, n74157_1_p4, n74157_1_p6, n74157_1_p7, n74157_1_p10,
       n74157_1_p11, n74157_1_p13, n74157_1_p14;

  // _7408 7408_1: pin names not known; wires that end beside it: S1, B0, n7408_1_p3, S1, B1, n7408_1_p6, 1'b1, S1, B3, n7408_1_p10, S1, B2, n7408_1_p13
  // _7432 7432_1: pin names not known; wires that end beside it: n7408_1_p3, A0, n7432_1_p3, n7408_1_p6, A1, n7432_1_p6, 1'b1, n7408_1_p10, A3, n7432_1_p10, n7408_1_p13, A2, n7432_1_p13
  // _7486 7486_1: pin names not known; wires that end beside it: S0, S1, n7486_1_p3, S1, S2, 1'b1
  // _7408 7408_2: pin names not known; wires that end beside it: S1, S2, n7408_2_p3, 1'b1
  // _74157 74157_1: pin names not known; wires that end beside it: S0, n7432_1_p3, n74157_1_p3, n74157_1_p4, n7432_1_p6, n74157_1_p6, n74157_1_p7, 1'b1, n7432_1_p10, n74157_1_p10, n74157_1_p11, n7432_1_p13, n74157_1_p13, n74157_1_p14
  // _7486 7486_2: pin names not known; wires that end beside it: A0, n7408_2_p3, n74157_1_p3, A1, n7408_2_p3, n74157_1_p6, 1'b1, A3, n7408_2_p3, n74157_1_p10, A2, n7408_2_p3, n74157_1_p13
  // _7432 7432_2: pin names not known; wires that end beside it: n7486_1_p3, n7408_2_p3, n7432_2_p3, 1'b1
  // _7483 7483_1: pin names not known; wires that end beside it: n74157_1_p11, n74157_1_p14, 1'b1, n74157_1_p7, n7432_2_p3, n74157_1_p4
endmodule
