// Logisim project B2_Group03.circ as structural Verilog: 3 circuits, main circuit main
module main (
  input  in_1,
  input  in_2,
  input  Data_Memory,
  input  in_4,
  output [7:0] out_5,
  output [7:0] out_6,
  output [3:0] out_7,
  output [3:0] sp,
  output [3:0] t4,
  output [3:0] t3,
  output [3:0] t2,
  output [3:0] t1,
  output [3:0] to
);

  wire branch_1_branch, control_main_1_alusrc, control_main_1_bneq, control_main_1_branch,
       control_main_1_jump, control_main_1_memread, control_main_1_memtoreg, control_main_1_memwrite,
       control_main_1_regdst, control_main_1_regwrite, main_1_p3;
  wire [2:0] control_main_1_aluop;
  wire [3:0] main_1_p5, multiplexer_3_out, multiplexer_4_out, multiplexer_5_out, ram_1_data, ram_2_data,
       registerfile_1_read_data1, registerfile_1_read_data2;
  wire [7:0] adder_1_out, adder_2_out, bit_extender_1_out, multiplexer_2_out;
  wire [11:4] ram_1_data_2;

  Register register_1 (.D(multiplexer_2_out), .Q(out_6), .clk(in_2), .clr(in_4));  // open: en
  Adder adder_1 (.a(out_6), .b(8'h1), .out(adder_1_out));  // open: cin, cout
  assign bit_extender_1_out = {{4{ram_1_data[3]}}, ram_1_data};  // Bit_Extender bit_extender_1
  RAM #(.dataWidth(16), .bus("asynch")) ram_1 (
    .addr(out_6), .data({out_7, ram_1_data_2, ram_1_data}), .sel(1'b1), .ld(1'b1));  // open: clr
  Multiplexer #(.width(8), .enable("false")) multiplexer_1 (
    .in0(adder_1_out), .in1(adder_2_out), .out(out_5), .sel(branch_1_branch));
  Adder adder_2 (.a(adder_1_out), .b(bit_extender_1_out), .out(adder_2_out));  // open: cin, cout
  control_main control_main_1 (
    .OpCode(out_7), .Jump(control_main_1_jump), .ALUop(control_main_1_aluop), .Bneq(control_main_1_bneq),
    .Branch(control_main_1_branch), .MemWrite(control_main_1_memwrite), .MemRead(control_main_1_memread),
    .RegWrite(control_main_1_regwrite), .MemToReg(control_main_1_memtoreg), .ALUsrc(control_main_1_alusrc),
    .RegDst(control_main_1_regdst));
  Multiplexer #(.width(8), .enable("false")) multiplexer_2 (
    .in0(out_5), .in1(ram_1_data_2), .out(multiplexer_2_out), .sel(control_main_1_jump));
  Multiplexer #(.width(4), .enable("false")) multiplexer_3 (
    .in0(ram_1_data_2[7:4]), .in1(ram_1_data), .out(multiplexer_3_out), .sel(control_main_1_regdst));
  branch branch_1 (.zero(main_1_p3), .beq(control_main_1_branch), .bne(control_main_1_bneq), .branch(branch_1_branch));
  RegisterFile registerfile_1 (
    .Src_Reg1(ram_1_data_2[11:8]), .Src_Reg2(ram_1_data_2[7:4]), .Dest_Reg(multiplexer_3_out),
    .Write_Data(multiplexer_5_out), .Read_Data1(registerfile_1_read_data1),
    .Read_Data2(registerfile_1_read_data2), .Reg_Write(control_main_1_regwrite), .t0(to), .t1(t1), .t2(t2),
    .t3(t3), .t4(t4), .sp(sp), .in_7(in_2), .in_1(in_1));  // open: zero
  Multiplexer #(.width(4), .enable("false")) multiplexer_4 (
    .in0(registerfile_1_read_data2), .in1(ram_1_data), .out(multiplexer_4_out), .sel(control_main_1_alusrc));
  // _4bitALU_main main_1: pin names not known; wires that end beside it: registerfile_1_read_data1, multiplexer_4_out, main_1_p3, control_main_1_aluop, main_1_p5
  RAM #(.addrWidth(4), .dataWidth(4), .bus("separate")) ram_2 (
    .addr(main_1_p5), .din(registerfile_1_read_data2), .data(ram_2_data), .str(control_main_1_memwrite),
    .sel(1'b1), .clk(in_2), .ld(control_main_1_memread), .clr(Data_Memory));
  Multiplexer #(.width(4), .enable("false")) multiplexer_5 (
    .in0(main_1_p5), .in1(ram_2_data), .out(multiplexer_5_out), .sel(control_main_1_memtoreg));
endmodule

module branch (
  input  zero,
  input  beq,
  input  bne,
  output branch
);

  wire n7404_1_p2, n7408_1_p3, n7408_1_p6;

  // _7404 7404_1: pin names not known; wires that end beside it: zero, n7404_1_p2, 1'b0, 1'b1
  // _7408 7408_1: pin names not known; wires that end beside it: zero, beq, n7408_1_p3, n7404_1_p2, bne, n7408_1_p6, 1'b1
  // _7432 7432_1: pin names not known; wires that end beside it: 1'b0, n7408_1_p6, n7408_1_p3, branch, 1'b0, 1'b1
endmodule

// Control Unit
module control_main (
  input  [3:0] OpCode,
  output Jump,
  output [2:0] ALUop,
  output Bneq,
  output Branch,
  output MemWrite,
  output MemRead,
  output RegWrite,
  output MemToReg,
  output ALUsrc,
  output RegDst
);

  ROM #(.addrWidth(4), .dataWidth(12)) rom_1 (
    .addr(OpCode), .data({RegDst, ALUsrc, MemToReg, RegWrite, MemRead, MemWrite, Branch, Bneq, ALUop, Jump}));  // open: sel

  // Notes on the sheet:
  //   contents of rom_1 (hex, n*v repeats v):
  //   902 904 1 36 444 26 506 784 50e 908 502 906 500 900 50c 504
endmodule
