// Logisim project Register File.circ as structural Verilog: 1 circuit, main circuit RegisterFile
module RegisterFile (
  input  in_1,
  input  Reg_Write,
  input  [3:0] Src_Reg1,
  input  [3:0] Src_Reg2,
  input  [3:0] Dest_Reg,
  input  [3:0] Write_Data,
  input  in_7,
  output [3:0] Read_Data1,
  output [3:0] Read_Data2,
  output [3:0] zero,
  output [3:0] t0,
  output [3:0] t1,
  output [3:0] t2,
  output [3:0] t3,
  output [3:0] t4,
  output [3:0] sp
);

  wire decoder_1_out0, decoder_1_out1, decoder_1_out2, decoder_1_out3, decoder_1_out4, decoder_1_out5,
       decoder_1_out6, n7408_1_p3, n7408_1_p6, n7408_1_p11, n7408_1_p14, n7408_2_p3, n7408_2_p6, n7408_2_p11;

  Decoder #(.select(3), .enable("false")) decoder_1 (
    .out0(decoder_1_out0), .out1(decoder_1_out1), .out2(decoder_1_out2), .out3(decoder_1_out3),
    .out4(decoder_1_out4), .out5(decoder_1_out5), .out6(decoder_1_out6), .sel(Dest_Reg[2:0]));  // open: out7
  // _7408 7408_1: pin names not known; wires that end beside it: decoder_1_out0, 1'b0, n7408_1_p3, decoder_1_out1, Reg_Write, n7408_1_p6, 1'b0, 1'b1, Reg_Write, decoder_1_out3, n7408_1_p11, Reg_Write, decoder_1_out2, n7408_1_p14
  // _7408 7408_2: pin names not known; wires that end beside it: decoder_1_out4, Reg_Write, n7408_2_p3, decoder_1_out5, Reg_Write, n7408_2_p6, 1'b0, 1'b1, Reg_Write, decoder_1_out6, n7408_2_p11
  Register #(.width(4)) u_zero (.D(Write_Data), .en(n7408_1_p3), .Q(zero), .clk(in_7), .clr(in_1));
  Register #(.width(4)) u_t0 (.D(Write_Data), .en(n7408_1_p6), .Q(t0), .clk(in_7), .clr(in_1));
  Register #(.width(4)) u_t1 (.D(Write_Data), .en(n7408_1_p14), .Q(t1), .clk(in_7), .clr(in_1));
  Register #(.width(4)) u_t2 (.D(Write_Data), .en(n7408_1_p11), .Q(t2), .clk(in_7), .clr(in_1));
  Register #(.width(4)) u_t3 (.D(Write_Data), .en(n7408_2_p3), .Q(t3), .clk(in_7), .clr(in_1));
  Register #(.width(4)) u_t4 (.D(Write_Data), .en(n7408_2_p6), .Q(t4), .clk(in_7), .clr(in_1));
  Register #(.width(4)) u_sp (.D(Write_Data), .en(n7408_2_p11), .Q(sp), .clk(in_7), .clr(in_1));
  Multiplexer #(.select(3), .width(4), .enable("false")) multiplexer_1 (
    .in0(zero), .in1(t0), .in2(t1), .in3(t2), .in4(t3), .in5(t4), .in6(sp), .out(Read_Data1),
    .sel(Src_Reg1[2:0]));  // open: in7
  Multiplexer #(.select(3), .width(4), .enable("false")) multiplexer_2 (
    .in0(zero), .in1(t0), .in2(t1), .in3(t2), .in4(t3), .in5(t4), .in6(sp), .out(Read_Data2),
    .sel(Src_Reg2[2:0]));  // open: in7
endmodule
